// Logisim project 16-bit Computer.circ as structural Verilog: 4 circuits, main circuit main
module main (
  input  [15:0] Bus_Override,
  input  in_2,
  input  [3:0] Op_Sel,
  input  Power,
  input  Manual_Override,
  input  in_6,
  input  in_7,
  input  in_8,
  input  in_9,
  input  in_10,
  input  in_11,
  input  in_12,
  input  in_13,
  input  in_14,
  input  in_15,
  input  in_16,
  input  in_17,
  input  in_18,
  output out_19,
  output out_20,
  output out_21,
  output out_22,
  output out_23,
  output out_24,
  output out_25,
  output out_26,
  output out_27,
  output out_28,
  output out_29,
  output out_30,
  output out_31,
  output out_32,
  output out_33,
  output out_34,
  output [15:0] out_35
);

  wire A_In, ALU_Out, AX_In, AX_Out, B_In, BP_In, BP_Out, button_1_out, button_2_out, button_3_out,
       button_4_out, button_5_out, button_6_out, button_7_out, button_8_out, button_9_out, button_10_out,
       button_11_out, button_12_out, button_13_out, button_14_out, button_15_out, BX_In, BX_Out, clock_1_out,
       comparator_1_eq, comparator_1_gt, comparator_1_lt, comparator_2_gt, comparator_2_lt, CX_In, CX_Out,
       decoder_1_out1, decoder_1_out2, decoder_1_out3, decoder_1_out4, decoder_1_out5, decoder_1_out6,
       decoder_1_out7, decoder_1_out8, decoder_1_out9, decoder_1_out10, DI_In, DI_Out, DX_In, DX_Out, Halt,
       I_In, JA_out, JB_out, JE_out, JG_out, JL_out, JNA_out, JNB_out, JNE_out, JNG_out, JNL_out,
       Manual_Tick_out, MAR_In, not_1_out, not_2_out, not_3_out, not_4_out, not_5_out, or_27_out, PC_Inc,
       PC_Out, PC_Set, RAM_In, RAM_Out, Reset_Counter, SI_In, SI_Out, SP_In, SP_Out;
  wire [3:0] I_q, I_q_2, I_q_3, I_q_4, or_1_out, rom_1_data, rom_1_data_2, rom_2_data_3;
  wire [4:0] counter_1_q;
  wire [15:0] A_q, alu_1_alu_out, and_1_out, and_2_out, and_3_out, and_4_out, and_5_out, and_6_out,
       and_7_out, and_8_out, and_9_out, and_10_out, and_11_out, and_12_out, AX_q, B_q, BP_2_q, BP_3_q,
       BP_4_q, BP_q, BX_q, CX_q, DX_q, MAR_q, or_8_out, or_33_out, ram_1_data;
  wire [19:0] rom_2_data;
  wire [31:20] rom_2_data_2;

  Button Manual_Tick (.out(Manual_Tick_out));
  assign and_1_out = Bus_Override & {16{in_2}};  // AND_Gate and_1, 16 bits wide
  assign or_1_out = Op_Sel;  // OR_Gate or_1, 4 bits wide OR_Gate
  Clock clock_1 (
    .Power(Power), .Manual_Override(Manual_Override), .Manual_Tick(Manual_Tick_out), .Halt(Halt),
    .Out(clock_1_out));
  or or_2 (AX_Out, rom_2_data[15], in_6);
  or or_3 (BX_Out, rom_2_data[16], in_10);
  or or_4 (CX_Out, rom_2_data[17], in_11);
  or or_5 (DX_Out, rom_2_data[18], in_13);
  or or_6 (Halt, rom_2_data[19], in_14);
  ALU alu_1 (.Operation(or_1_out), .A(A_q), .B(B_q), .ALU_Out(alu_1_alu_out));
  Register #(.width(16), .trigger("falling")) A (
    .D({out_19, out_20, out_21, out_22, out_23, out_24, out_25, out_26, out_27, out_28, out_29, out_30, out_31, out_32, out_33, out_34}),
    .Q(A_q), .clk(A_In));  // open: en, clr
  Register #(.width(16), .trigger("falling")) B (
    .D({out_19, out_20, out_21, out_22, out_23, out_24, out_25, out_26, out_27, out_28, out_29, out_30, out_31, out_32, out_33, out_34}),
    .Q(B_q), .clk(B_In));  // open: en, clr
  Register #(.width(16), .trigger("falling")) I (
    .D({out_19, out_20, out_21, out_22, out_23, out_24, out_25, out_26, out_27, out_28, out_29, out_30, out_31, out_32, out_33, out_34}),
    .Q({I_q_4, I_q_3, I_q_2, I_q}), .clk(I_In));  // open: en, clr
  Counter #(.width(5), .max('h10)) counter_1 (
    .Q(counter_1_q), .clk(clock_1_out), .clr(Reset_Counter));  // open: load, D, count, carry
  ROM #(.addrWidth(5)) rom_1 (.addr(counter_1_q), .data({rom_1_data, rom_1_data_2}));  // open: sel
  ROM #(.addrWidth(20), .dataWidth(32)) rom_2 (
    .addr({I_q_4, I_q_3, I_q_2, I_q, rom_1_data}),
    .data({rom_2_data_2[31:28], rom_2_data_3, rom_2_data_2[23:20], rom_2_data}));  // open: sel
  assign {out_19, out_20, out_21, out_22, out_23, out_24, out_25, out_26, out_27, out_28, out_29, out_30, out_31, out_32, out_33, out_34} = and_1_out | and_7_out | and_2_out | and_8_out | or_8_out;  // OR_Gate or_7, 16 bits wide
  assign and_2_out = {16{ALU_Out}} & alu_1_alu_out;  // AND_Gate and_2, 16 bits wide
  Comparator #(.width(16), .mode("unsigned")) comparator_1 (
    .a(A_q), .b(B_q), .gt(comparator_1_gt), .eq(comparator_1_eq), .lt(comparator_1_lt));
  Comparator #(.width(16)) comparator_2 (.a(A_q), .b(B_q), .gt(comparator_2_gt), .lt(comparator_2_lt));  // open: eq
  not not_1 (not_1_out, comparator_2_lt);
  Button button_1 (.out(button_1_out));
  Button button_2 (.out(button_2_out));
  Button button_3 (.out(button_3_out));
  Button button_4 (.out(button_4_out));
  Button button_5 (.out(button_5_out));
  Button button_6 (.out(button_6_out));
  assign or_8_out = and_3_out | and_4_out | or_33_out | and_5_out | and_6_out;  // OR_Gate or_8, 16 bits wide
  not not_2 (not_2_out, comparator_1_gt);
  not not_3 (not_3_out, comparator_1_eq);
  not not_4 (not_4_out, comparator_1_lt);
  not not_5 (not_5_out, comparator_2_gt);
  Decoder #(.select(4), .disabled(0), .enable("false")) decoder_1 (
    .out1(decoder_1_out1), .out2(decoder_1_out2), .out3(decoder_1_out3), .out4(decoder_1_out4),
    .out5(decoder_1_out5), .out6(decoder_1_out6), .out7(decoder_1_out7), .out8(decoder_1_out8),
    .out9(decoder_1_out9), .out10(decoder_1_out10), .sel(rom_2_data_2[31:28]));  // open: out0, out11, out12, out13, out14, out15
  or or_9 (ALU_Out, rom_2_data[10], in_7);
  or or_10 (AX_In, rom_2_data[11], button_1_out);
  or or_11 (BX_In, rom_2_data[12], button_2_out);
  or or_12 (CX_In, rom_2_data[13], button_3_out);
  or or_13 (DX_In, rom_2_data[14], button_4_out);
  or or_14 (SI_Out, rom_2_data_3[0], in_15);
  or or_15 (SI_In, rom_2_data_3[1], button_5_out);
  or or_16 (DI_Out, rom_2_data_3[2], in_17);
  or or_17 (DI_In, rom_2_data_3[3], button_6_out);
  assign and_3_out = {16{DX_Out}} & DX_q;  // AND_Gate and_3, 16 bits wide
  assign and_4_out = {16{CX_Out}} & CX_q;  // AND_Gate and_4, 16 bits wide
  assign and_5_out = {16{BX_Out}} & BX_q;  // AND_Gate and_5, 16 bits wide
  assign and_6_out = {16{AX_Out}} & AX_q;  // AND_Gate and_6, 16 bits wide
  assign and_7_out = {16{PC_Out}} & out_35;  // AND_Gate and_7, 16 bits wide
  Register #(.width(16), .trigger("falling")) MAR (
    .D({out_19, out_20, out_21, out_22, out_23, out_24, out_25, out_26, out_27, out_28, out_29, out_30, out_31, out_32, out_33, out_34}),
    .Q(MAR_q), .clk(MAR_In));  // open: en, clr
  Register #(.width(16), .trigger("falling")) AX (
    .D({out_19, out_20, out_21, out_22, out_23, out_24, out_25, out_26, out_27, out_28, out_29, out_30, out_31, out_32, out_33, out_34}),
    .Q(AX_q), .clk(AX_In));  // open: en, clr
  PC pc_1 (
    .Set(PC_Set),
    .PC_Data({out_19, out_20, out_21, out_22, out_23, out_24, out_25, out_26, out_27, out_28, out_29, out_30, out_31, out_32, out_33, out_34}),
    .Increment(PC_Inc), .PC_Out(out_35));
  Button button_7 (.out(button_7_out));
  Button button_8 (.out(button_8_out));
  Button button_9 (.out(button_9_out));
  Button button_10 (.out(button_10_out));
  Button button_11 (.out(button_11_out));
  Button button_12 (.out(button_12_out));
  Register #(.width(16), .trigger("falling")) BX (
    .D({out_19, out_20, out_21, out_22, out_23, out_24, out_25, out_26, out_27, out_28, out_29, out_30, out_31, out_32, out_33, out_34}),
    .Q(BX_q), .clk(BX_In));  // open: en, clr
  assign and_8_out = {16{RAM_Out}} & ram_1_data;  // AND_Gate and_8, 16 bits wide
  RAM #(.addrWidth(16), .dataWidth(16), .bus("separate")) ram_1 (
    .addr(MAR_q),
    .din({out_19, out_20, out_21, out_22, out_23, out_24, out_25, out_26, out_27, out_28, out_29, out_30, out_31, out_32, out_33, out_34}),
    .data(ram_1_data), .clk(RAM_In));  // open: str, sel, ld, clr
  and JA (JA_out, comparator_1_gt, decoder_1_out1);
  and JNA (JNA_out, not_2_out, decoder_1_out2);
  and JE (JE_out, comparator_1_eq, decoder_1_out3);
  and JNE (JNE_out, not_3_out, decoder_1_out4);
  and JB (JB_out, comparator_1_lt, decoder_1_out5);
  and JNB (JNB_out, not_4_out, decoder_1_out6);
  and JG (JG_out, comparator_2_gt, decoder_1_out7);
  and JNG (JNG_out, not_5_out, decoder_1_out8);
  and JL (JL_out, comparator_2_lt, decoder_1_out9);
  and JNL (JNL_out, not_1_out, decoder_1_out10);
  or or_18 (PC_Set, rom_2_data[5], in_8);
  or or_19 (RAM_In, rom_2_data[6], button_7_out);
  or or_20 (Reset_Counter, rom_2_data[7], button_8_out);
  or or_21 (A_In, rom_2_data[8], button_9_out);
  or or_22 (B_In, rom_2_data[9], button_10_out);
  or or_23 (BP_Out, rom_2_data_2[20], in_16);
  or or_24 (BP_In, rom_2_data_2[21], button_11_out);
  or or_25 (SP_Out, rom_2_data_2[22], in_18);
  or or_26 (SP_In, rom_2_data_2[23], button_12_out);
  Register #(.width(16), .trigger("falling")) DX (
    .D({out_19, out_20, out_21, out_22, out_23, out_24, out_25, out_26, out_27, out_28, out_29, out_30, out_31, out_32, out_33, out_34}),
    .Q(DX_q), .clk(DX_In));  // open: en, clr
  Register #(.width(16), .trigger("falling")) CX (
    .D({out_19, out_20, out_21, out_22, out_23, out_24, out_25, out_26, out_27, out_28, out_29, out_30, out_31, out_32, out_33, out_34}),
    .Q(CX_q), .clk(CX_In));  // open: en, clr
  or or_27 (or_27_out, JA_out, JNA_out, JE_out, JNE_out, JB_out, JNB_out, JG_out, JNG_out, JL_out, JNL_out);
  Register #(.width(16), .trigger("falling")) BP (
    .D({out_19, out_20, out_21, out_22, out_23, out_24, out_25, out_26, out_27, out_28, out_29, out_30, out_31, out_32, out_33, out_34}),
    .Q(BP_q), .clk(BP_In));  // open: en, clr
  Register #(.width(16), .trigger("falling")) BP_2 (
    .D({out_19, out_20, out_21, out_22, out_23, out_24, out_25, out_26, out_27, out_28, out_29, out_30, out_31, out_32, out_33, out_34}),
    .Q(BP_2_q), .clk(BP_In));  // open: en, clr
  Register #(.width(16), .trigger("falling")) BP_3 (
    .D({out_19, out_20, out_21, out_22, out_23, out_24, out_25, out_26, out_27, out_28, out_29, out_30, out_31, out_32, out_33, out_34}),
    .Q(BP_3_q), .clk(BP_In));  // open: en, clr
  Register #(.width(16), .trigger("falling")) BP_4 (
    .D({out_19, out_20, out_21, out_22, out_23, out_24, out_25, out_26, out_27, out_28, out_29, out_30, out_31, out_32, out_33, out_34}),
    .Q(BP_4_q), .clk(BP_In));  // open: en, clr
  Button button_13 (.out(button_13_out));
  Button button_14 (.out(button_14_out));
  Button button_15 (.out(button_15_out));
  assign and_9_out = BP_q & {16{BP_Out}};  // AND_Gate and_9, 16 bits wide
  assign and_10_out = BP_2_q & {16{BP_Out}};  // AND_Gate and_10, 16 bits wide
  assign and_11_out = BP_3_q & {16{BP_Out}};  // AND_Gate and_11, 16 bits wide
  assign and_12_out = BP_4_q & {16{BP_Out}};  // AND_Gate and_12, 16 bits wide
  or or_28 (PC_Out, rom_2_data[0], rom_1_data_2[0], in_9);
  or or_29 (MAR_In, rom_2_data[1], rom_1_data_2[1], button_13_out);
  or or_30 (RAM_Out, rom_2_data[2], rom_1_data_2[2], in_12);
  or or_31 (I_In, rom_2_data[3], rom_1_data_2[3], button_14_out);
  or or_32 (PC_Inc, rom_1_data_2[3], rom_2_data[4], button_15_out, or_27_out);
  assign or_33_out = and_9_out | and_10_out | and_11_out | and_12_out;  // OR_Gate or_33, 16 bits wide

  // Notes on the sheet:
  //   Micro Instructions
  //   Micro Controller
  //   contents of rom_1 (hex, n*v repeats v):
  //   3 c 10 20 30 40 50 60 70 80 90 a0 b0 c0 d0 e0 f0
  //   contents of rom_2 (hex, n*v repeats v):
  //   0 80 511*0 814 80 14*0 1014 80 14*0 2014 80 14*0 4014 80 14*0 200014 80 14*0 800014 80 14*0 2000014
  //   80 14*0 8000014 80 142*0 16 804 80 13*0 16 1004 80 13*0 16 2004 80 13*0 16 4004 80 13*0 16 200004 80
  //   13*0 16 800004 80 13*0 16 2000004 80 13*0 16 8000004 80 141*0 16 8040 80 13*0 16 10040 80 13*0 16
  //   20040 80 13*0 16 40040 80 13*0 16 100040 80 13*0 16 400040 80 13*0 16 1000040 80 13*0 16 4000040 80
  //   2957*0 8800 80 14*0 10800 80 14*0 20800 80 14*0 40800 80 14*0 100800 80 14*0 400800 80 14*0 1000800
  //   80 14*0 4000800 80 142*0 9000 80 14*0 11000 80 14*0 21000 80 14*0 41000 80 14*0 101000 80 14*0
  //   401000 80 14*0 1001000 80 14*0 4001000 80 142*0 a000 80 14*0 12000 80 14*0 22000 80 14*0 42000 80
  //   14*0 102000 80 14*0 402000 80 14*0 1002000 80 14*0 4002000 80 142*0 c000 80 14*0 14000 80 14*0 24000
  //   80 14*0 44000 80 14*0 104000 80 14*0 404000 80 14*0 1004000 80 14*0 4004000 80 142*0 208000 80 14*0
  //   210000 80 14*0 220000 80 14*0 240000 80 14*0 300000 80 14*0 600000 80 14*0 1200000 80 14*0 4200000
  //   80 142*0 808000 80 14*0 810000 80 14*0 820000 80 14*0 840000 80 14*0 900000 80 14*0 c00000 80 14*0
  //   1800000 80 14*0 4800000 80 142*0 2008000 80 14*0 2010000 80 14*0 2020000 80 14*0 2040000 80 14*0
  //   2100000 80 14*0 2400000 80 14*0 3000000 80 14*0 6000000 80 142*0 8008000 80 14*0 8010000 80 14*0
  //   8020000 80 14*0 8040000 80 14*0 8100000 80 14*0 8400000 80 14*0 9000000 80 14*0 c000000 80 2190*0
  //   8002 804 80 13*0 10002 804 80 13*0 20002 804 80 13*0 40002 804 80 13*0 100002 804 80 13*0 400002 804
  //   80 13*0 1000002 804 80 13*0 4000002 804 80 141*0 8002 1004 80 13*0 10002 1004 80 13*0 20002 1004 80
  //   13*0 40002 1004 80 13*0 100002 1004 80 13*0 400002 1004 80 13*0 1000002 1004 80 13*0 4000002 1004 80
  //   141*0 8002 2004 80 13*0 10002 2004 80 13*0 20002 2004 80 13*0 40002 2004 80 13*0 100002 2004 80 13*0
  //   400002 2004 80 13*0 1000002 2004 80 13*0 4000002 2004 80 141*0 8002 4004 80 13*0 10002 4004 80 13*0
  //   20002 4004 80 13*0 40002 4004 80 13*0 100002 4004 80 13*0 400002 4004 80 13*0 1000002 4004 80 13*0
  //   4000002 4004 80 141*0 8002 200004 80 13*0 10002 200004 80 13*0 20002 200004 80 13*0 40002 200004 80
  //   13*0 100002 200004 80 13*0 400002 200004 80 13*0 1000002 200004 80 13*0 4000002 200004 80 141*0 8002
  //   800004 80 13*0 10002 800004 80 13*0 20002 800004 80 13*0 40002 800004 80 13*0 100002 800004 80 13*0
  //   400002 800004 80 13*0 1000002 800004 80 13*0 4000002 800004 80 141*0 8002 2000004 80 13*0 10002
  //   2000004 80 13*0 20002 2000004 80 13*0 40002 2000004 80 13*0 100002 2000004 80 13*0 400002 2000004 80
  //   13*0 1000002 2000004 80 13*0 4000002 2000004 80 141*0 8002 8000004 80 13*0 10002 8000004 80 13*0
  //   20002 8000004 80 13*0 40002 8000004 80 13*0 100002 8000004 80 13*0 400002 8000004 80 13*0 1000002
  //   8000004 80 13*0 4000002 8000004 80 2189*0 8002 8040 80 13*0 8002 10040 80 29*0 8002 40040 80 13*0
  //   8002 100040 80 13*0 8002 400040 80 13*0 8002 1000040 80 13*0 8002 4000040 80 141*0 10002 8040 80
  //   13*0 10002 10040 80 29*0 10002 40040 80 13*0 10002 100040 80 13*0 10002 400040 80 13*0 10002 1000040
  //   80 13*0 10002 4000040 80 141*0 20002 8040 80 13*0 20002 10040 80 29*0 20002 40040 80 13*0 20002
  //   100040 80 13*0 20002 400040 80 13*0 20002 1000040 80 13*0 20002 4000040 80 141*0 40002 8040 80 13*0
  //   40002 10040 80 29*0 40002 40040 80 13*0 40002 100040 80 13*0 40002 400040 80 13*0 40002 1000040 80
  //   13*0 40002 4000040 80 141*0 100002 8040 80 13*0 100002 10040 80 29*0 100002 40040 80 13*0 100002
  //   100040 80 13*0 100002 400040 80 13*0 100002 1000040 80 13*0 100002 4000040 80 141*0 400002 8040 80
  //   13*0 400002 10040 80 29*0 400002 40040 80 13*0 400002 100040 80 13*0 400002 400040 80 13*0 400002
  //   1000040 80 13*0 400002 4000040 80 141*0 1000002 8040 80 13*0 1000002 10040 80 29*0 1000002 40040 80
  //   13*0 1000002 100040 80 13*0 1000002 400040 80 13*0 1000002 1000040 80 13*0 1000002 4000040 80 141*0
  //   4000002 8040 80 13*0 4000002 10040 80 29*0 4000002 40040 80 13*0 4000002 100040 80 13*0 4000002
  //   400040 80 13*0 4000002 1000040 80 13*0 4000002 4000040 80
  //   RAM
endmodule

module Clock (
  input  Power,
  input  Manual_Override,
  input  Manual_Tick,
  input  Halt,
  output Out
);

  wire and_1_out, and_2_out, clock_1_out, not_1_out, not_2_out, or_1_out;

  Clock_part clock_1 (.out(clock_1_out));
  not not_1 (not_1_out, Manual_Override);
  and and_1 (and_1_out, not_1_out, clock_1_out);
  and and_2 (and_2_out, Manual_Override, Manual_Tick);
  or or_1 (or_1_out, and_1_out, and_2_out);
  not not_2 (not_2_out, Halt);
  and and_3 (Out, Power, not_2_out, or_1_out);
endmodule

module ALU (
  input  [3:0] Operation,
  input  [15:0] A,
  input  [15:0] B,
  output [15:0] ALU_Out
);

  wire [15:0] adder_1_out, and_1_out, divider_1_out, multiplier_1_out, nand_1_out, nor_1_out, not_1_out,
       or_1_out, shifter_1_out, shifter_2_out, shifter_3_out, shifter_4_out, shifter_5_out, subtractor_1_out,
       xnor_1_out, xor_1_out;

  Adder #(.width(16)) adder_1 (.a(A), .b(B), .out(adder_1_out));  // open: cin, cout
  Subtractor #(.width(16)) subtractor_1 (.a(A), .b(B), .out(subtractor_1_out));  // open: bin, bout
  Multiplier #(.width(16)) multiplier_1 (.a(A), .b(B), .out(multiplier_1_out));  // open: cin, cout
  Divider #(.width(16)) divider_1 (.a(A), .b(B), .out(divider_1_out));  // open: upper, rem
  Shifter #(.width(16)) shifter_1 (.in(A), .\dist (B[3:0]), .out(shifter_1_out));
  Shifter #(.width(16), .shift("lr")) shifter_2 (.in(A), .\dist (B[3:0]), .out(shifter_2_out));
  Shifter #(.width(16), .shift("ar")) shifter_3 (.in(A), .\dist (B[3:0]), .out(shifter_3_out));
  Shifter #(.width(16), .shift("rl")) shifter_4 (.in(A), .\dist (B[3:0]), .out(shifter_4_out));
  Shifter #(.width(16), .shift("rr")) shifter_5 (.in(A), .\dist (B[3:0]), .out(shifter_5_out));
  assign and_1_out = A & B;  // AND_Gate and_1, 16 bits wide
  assign or_1_out = A | B;  // OR_Gate or_1, 16 bits wide
  assign xor_1_out = A ^ B;  // XOR_Gate xor_1, 16 bits wide
  assign not_1_out = ~A;  // NOT_Gate not_1, 16 bits wide
  assign nand_1_out = ~(A & B);  // NAND_Gate nand_1, 16 bits wide
  assign nor_1_out = ~(A | B);  // NOR_Gate nor_1, 16 bits wide
  assign xnor_1_out = ~(A ^ B);  // XNOR_Gate xnor_1, 16 bits wide
  Multiplexer #(.select(4), .width(16), .disabled(0), .enable("false")) multiplexer_1 (
    .in0(adder_1_out), .in1(subtractor_1_out), .in2(multiplier_1_out), .in3(divider_1_out),
    .in4(shifter_1_out), .in5(shifter_2_out), .in6(shifter_3_out), .in7(shifter_4_out), .in8(shifter_5_out),
    .in9(and_1_out), .in10(or_1_out), .in11(xor_1_out), .in12(not_1_out), .in13(nand_1_out),
    .in14(nor_1_out), .in15(xnor_1_out), .out(ALU_Out), .sel(Operation));
endmodule

module PC (
  input  Set,
  input  [15:0] PC_Data,
  input  Increment,
  output [15:0] PC_Out
);

  wire or_1_out;
  wire [15:0] adder_1_out, multiplexer_1_out;

  Adder #(.width(16)) adder_1 (.a(PC_Out), .b(16'h1), .out(adder_1_out));  // open: cin, cout
  Multiplexer #(.width(16), .disabled(0), .enable("false")) multiplexer_1 (
    .in0(adder_1_out), .in1(PC_Data), .out(multiplexer_1_out), .sel(Set));
  or or_1 (or_1_out, Set, Increment);
  Register #(.width(16), .trigger("falling")) register_1 (
    .D(multiplexer_1_out), .Q(PC_Out), .clk(or_1_out));  // open: en, clr
endmodule
